# Fritzing sketch master (saved by Fritzing 0.8.3b)
breadboards: 1

parts:
  Part1 = Arduino Uno (Rev3)
  R1 = Resistor [tolerance=±5% resistance=1k package=THT]
  R2 = Resistor [tolerance=±5% resistance=1k package=THT]
  Part2 = Breakout Board for Electret Microphone
  PIR1 = PIR sensor

nets:
  N1: Part1.A0, Part2.AUD
  N2: Part1.A4/SDA, R1.Pin_1
  N3: Part1.A5/SCL, R2.Pin_1
  5V: Part1.5V, R1.Pin_0, R2.Pin_0, Part2.VCC, PIR1.SIG
  N4: Part1.ICSP_SCK, Part1.D13/SCK, PIR1.VDD
  GND: Part1.GND, Part2.GND, PIR1.GND

notes:
  Power +
  Power -
  I2C-A4
  I2C-A5
  LED Strips
