# Fritzing sketch sound_and_light (saved by Fritzing 0.7.4b)
breadboards: 1

parts:
  Arduino1 = Arduino
  Part1 = Breakout Board for Electret Microphone
  R1 = Resistor [tolerance=±5% resistance=4.7k package=THT]

nets:
  +5V: Arduino1.+5V, Part1.VCC
  N1: Arduino1.GND, R1.Pin_0
  N2: Arduino1.A1, Part1.AUD
  N3: Part1.GND, R1.Pin_1

notes:
  The location of the pinholes on the mic breakout board do not match those of the “virtual” breakout board here; however, the connections are correct (wires connected to GND on the real breakout board are also connected to GND on the board here). Be sure to verify the connections before powering!
